# Fritzing sketch Bolt IoT multiplexed (saved by Fritzing 0.9.10b)
breadboards: 1

parts:
  B1 = Bolt WiFi Module [package=dip]
  T1 = LM35 Temperature Sensor [package="TO92 [THT]"]
  R1 = Photocell (LDR) [package=THT]
  R2 = Resistor [tolerance=±5% power=0.25 resistance=220 package=THT]
  Part1 = Soil Moisture Sensor

nets:
  GND: B1.pin1, T1.GND, R2.Pin_1, Part1.GND
  N1: B1.pin6, T1.+Vs
  N2: B1.pin7, T1.Vout, R1.pin_1, R2.Pin_0, Part1.SIG

custom parts:
  Bolt WiFi Module: Bolt IoT platform gives you the capability to control your devices and collect data from IoT devices safely and securely no matter where you are. Get actionable insights by deploying machine learning algorithms with just a few clicks to detect anomalies as well as predict sensor values.
